// Logisim project J.circ as structural Verilog: 1 circuit, main circuit main
module main (
  input  in_1,
  input  in_2,
  input  in_3,
  input  in_4,
  input  in_5,
  input  in_6,
  input  in_7,
  input  in_8,
  output out_9,
  output out_10,
  output out_11,
  output out_12,
  output out_13,
  output out_14
);

  wire and_1_out, nand_1_out, nor_1_out, or_1_out, transistor_1_out, transistor_2_out, transistor_7_out;

  and and_1 (and_1_out, in_1, in_2);
  nor nor_1 (nor_1_out, in_1, in_2);
  nor nor_2 (out_9, and_1_out, nor_1_out);
  or or_1 (or_1_out, in_5, in_6);
  nand nand_1 (nand_1_out, in_5, in_6);
  nand nand_2 (out_12, or_1_out, nand_1_out);
  Transistor transistor_1 (.in(1'b1), .out(transistor_1_out), .gate(in_3));
  Transistor transistor_2 (.in(transistor_1_out), .out(transistor_2_out), .gate(in_4));
  Transistor #(.\type ("n")) transistor_3 (.in(1'b0), .out(transistor_2_out), .gate(in_3));
  Transistor #(.\type ("n")) transistor_4 (.in(1'b0), .out(transistor_2_out), .gate(in_4));
  Transistor transistor_5 (.in(in_8), .out(out_14), .gate(in_7));
  Transistor #(.\type ("n")) transistor_6 (.in(transistor_7_out), .out(out_14), .gate(in_7));
  Transistor transistor_7 (.in(1'b1), .out(transistor_7_out), .gate(in_8));
  Transistor #(.\type ("n")) transistor_8 (.in(1'b0), .out(transistor_7_out), .gate(in_8));
  // Transmission_Gate transmission_1: pin names not known; wires that end beside it: out_14, in_8, transistor_7_out, in_7
  Transistor transistor_9 (.in(1'b1), .out(out_11), .gate(transistor_2_out));
  Transistor #(.\type ("n")) transistor_10 (.in(1'b0), .out(out_11), .gate(transistor_2_out));
endmodule
